// Logisim project Taller1-Logica-Combinatorios.circ as structural Verilog: 9 circuits, main circuit verificador
module sumador_simple (
  input  A,
  input  B,
  output S,
  output Cout
);

  xor xor_1 (S, A, B);
  and and_1 (Cout, A, B);
endmodule

module sumador_completo (
  input  Cin,
  input  A,
  input  B,
  output S,
  output Cout
);

  wire sumador_simple_1_cout, sumador_simple_1_s, sumador_simple_2_cout;

  sumador_simple sumador_simple_1 (.A(A), .B(B), .S(sumador_simple_1_s), .Cout(sumador_simple_1_cout));
  sumador_simple sumador_simple_2 (.A(Cin), .B(sumador_simple_1_s), .S(S), .Cout(sumador_simple_2_cout));
  or or_1 (Cout, sumador_simple_2_cout, sumador_simple_1_cout);
endmodule

module sumador_4 (
  input  Cin,
  input  [3:0] A,
  input  [3:0] B,
  output [3:0] S,
  output Cout
);

  wire sumador_completo_1_cout, sumador_completo_2_cout, sumador_completo_3_cout;

  sumador_completo sumador_completo_1 (.Cin(Cin), .A(A[0]), .B(B[0]), .S(S[0]), .Cout(sumador_completo_1_cout));
  sumador_completo sumador_completo_2 (
    .Cin(sumador_completo_1_cout), .A(A[1]), .B(B[1]), .S(S[1]), .Cout(sumador_completo_2_cout));
  sumador_completo sumador_completo_3 (
    .Cin(sumador_completo_2_cout), .A(A[2]), .B(B[2]), .S(S[2]), .Cout(sumador_completo_3_cout));
  sumador_completo sumador_completo_4 (.Cin(sumador_completo_3_cout), .A(A[3]), .B(B[3]), .S(S[3]), .Cout(Cout));
  Hex_Digit_Display hex_digit_display_1 (.value(S));  // open: dp
endmodule

module comparador_cero (
  input  [3:0] A,
  output Z
);

  wire and_1_out, and_2_out, not_1_out, not_2_out, not_3_out, not_4_out;

  not not_1 (not_1_out, A[0]);
  not not_2 (not_2_out, A[1]);
  not not_3 (not_3_out, A[2]);
  not not_4 (not_4_out, A[3]);
  and and_1 (and_1_out, not_1_out, not_4_out);
  and and_2 (and_2_out, not_3_out, not_2_out);
  and and_3 (Z, and_1_out, and_2_out);
endmodule

module sumador_flags (
  input  Cin,
  input  [3:0] A,
  input  [3:0] B,
  output Z,
  output [3:0] S,
  output N,
  output C,
  output V
);

  wire not_1_out, xor_1_out, xor_2_out;

  xor xor_1 (xor_1_out, B[3], A[3]);
  sumador_4 sumador_4_1 (.Cin(Cin), .A(A), .B(B), .S({N, S[2:0]}), .Cout(C));
  not not_1 (not_1_out, xor_1_out);
  comparador_cero comparador_cero_1 (.A({N, S[2:0]}), .Z(Z));
  and and_1 (V, not_1_out, xor_2_out);
  Hex_Digit_Display hex_digit_display_1 (.value({N, S[2:0]}));  // open: dp
  xor xor_2 (xor_2_out, N, B[3]);

  assign S[3] = N;
endmodule

module incrementador_4 (
  input  [3:0] A,
  output [3:0] S
);

  wire sumador_simple_1_cout, sumador_simple_2_cout;

  not not_1 (S[0], A[0]);
  sumador_simple sumador_simple_1 (.A(A[0]), .B(A[1]), .S(S[1]), .Cout(sumador_simple_1_cout));
  sumador_simple sumador_simple_2 (.A(sumador_simple_1_cout), .B(A[2]), .S(S[2]), .Cout(sumador_simple_2_cout));
  sumador_simple sumador_simple_3 (.A(sumador_simple_2_cout), .B(A[3]), .S(S[3]));  // open: Cout
  Hex_Digit_Display hex_digit_display_1 (.value(S));  // open: dp
endmodule

module inversor_4 (
  input  [3:0] A,
  input  INV,
  output [3:0] S
);

  wire [3:0] incrementador_4_1_s, not_1_out;

  assign not_1_out = ~A;  // NOT_Gate not_1, 4 bits wide
  incrementador_4 incrementador_4_1 (.A(not_1_out), .S(incrementador_4_1_s));
  Multiplexer #(.width(4)) multiplexer_1 (.in0(A), .in1(incrementador_4_1_s), .out(S), .sel(INV));
  Hex_Digit_Display hex_digit_display_1 (.value(S));  // open: dp
endmodule

module ALU (
  input  [3:0] A,
  input  [3:0] B,
  input  [1:0] OP,
  output N,
  output Z,
  output V,
  output C,
  output [3:0] S
);

  wire comparador_cero_1_z, comparador_cero_2_z, comparador_cero_3_z, not_1_out, sumador_flags_1_c,
       sumador_flags_1_n, sumador_flags_1_v, sumador_flags_1_z, sumador_flags_2_c, sumador_flags_2_n,
       sumador_flags_2_v, sumador_flags_2_z, xor_1_out;
  wire [3:0] and_1_out, inversor_4_1_s, or_1_out, sumador_flags_1_s, sumador_flags_2_s;

  assign and_1_out = A & B;  // AND_Gate and_1, 4 bits wide
  assign or_1_out = A | B;  // OR_Gate or_1, 4 bits wide
  sumador_flags sumador_flags_1 (
    .A(A), .B(B), .Z(sumador_flags_1_z), .S(sumador_flags_1_s), .N(sumador_flags_1_n), .C(sumador_flags_1_c),
    .V(sumador_flags_1_v));  // open: Cin
  inversor_4 inversor_4_1 (.A(B), .INV(1'b1), .S(inversor_4_1_s));
  comparador_cero comparador_cero_1 (.A(B), .Z(comparador_cero_1_z));
  xor xor_1 (xor_1_out, comparador_cero_1_z, not_1_out);
  sumador_flags sumador_flags_2 (
    .A(A), .B(inversor_4_1_s), .Z(sumador_flags_2_z), .S(sumador_flags_2_s), .N(sumador_flags_2_n),
    .C(sumador_flags_2_c), .V(sumador_flags_2_v));  // open: Cin
  not not_1 (not_1_out, sumador_flags_2_c);
  Multiplexer #(.select(2), .width(4)) multiplexer_1 (
    .in0(sumador_flags_1_s), .in1(sumador_flags_2_s), .in2(and_1_out), .in3(or_1_out), .out(S), .sel(OP));
  Multiplexer #(.select(2)) multiplexer_2 (
    .in0(sumador_flags_1_v), .in1(sumador_flags_2_v), .in2(1'b0), .in3(1'b0), .out(V), .sel(OP));
  Multiplexer #(.select(2)) multiplexer_3 (
    .in0(sumador_flags_1_c), .in1(xor_1_out), .in2(1'b0), .in3(1'b0), .out(C), .sel(OP));
  Hex_Digit_Display hex_digit_display_1 (.value(S));  // open: dp
  Multiplexer #(.select(2)) multiplexer_4 (
    .in0(sumador_flags_1_z), .in1(sumador_flags_2_z), .in2(comparador_cero_2_z), .in3(comparador_cero_3_z),
    .out(Z), .sel(OP));
  Multiplexer #(.select(2)) multiplexer_5 (
    .in0(sumador_flags_1_n), .in1(sumador_flags_2_n), .in2(S[3]), .in3(S[3]), .out(N), .sel(OP));
  comparador_cero comparador_cero_2 (.A(and_1_out), .Z(comparador_cero_2_z));
  comparador_cero comparador_cero_3 (.A(or_1_out), .Z(comparador_cero_3_z));
endmodule

module verificador (
  output [3:0] out_1,
  output [3:0] out_2,
  output [1:0] out_3,
  output halt,
  output N,
  output Z,
  output V,
  output C,
  output [3:0] res
);

  wire clock_1_out;

  Clock clock_1 (.out(clock_1_out));
  Counter #(.max('h3ff), .width(10)) counter_1 (
    .clk(clock_1_out), .carry(halt), .Q({out_3, out_2, out_1}));  // open: clr, load, up, count, D
  ALU alu_1 (.A(out_1), .B(out_2), .OP(out_3), .N(N), .Z(Z), .V(V), .C(C), .S(res));
endmodule
